# Fritzing sketch arduino (saved by Fritzing 0.8.7b)
breadboards: 1

parts:
  Part1 = Arduino Uno (Rev3)
  U1 = 7-SEGMENT-4DIGIT [package=7-segment-4digit_longpads_for_pogobed]
  Part2 = Triple Axis Gyro Breakout ITG-3200
  U2 = 7-SEGMENT-4DIGIT [package=7-segment-4digit_longpads_for_pogobed]
  Part3 = IR Receiver Breakout [package=PCB]
  J1 = Piezo Speaker
  Q1 = NPN-Transistor [package="TO92 [THT]"]
  Part5 = Real Time Clock Module - DS1307 RTC Breakout Board  # not connected
  R1 = Resistor [tolerance=±5% resistance=10k package="1206 [SMD]"]
  R2 = Resistor [tolerance=±5% resistance=220 package=THT]
  R3 = Resistor [tolerance=±5% resistance=100 package="0805 [SMD]"]
  LED1 = LED - 5mm [color="Red (633nm)" package="5 mm [THT]"]

nets:
  N1: Part1.A4/SDA, Part2.SDA
  N2: Part1.D8, U2.4
  N3: Part1.D9_PWM, U2.3
  N4: Part1.D12/MISO, R1.Pin_0
  N5: Part1.D4, U1.4
  N6: Part1.D5_PWM, U1.3
  N7: Part1.D6_PWM, R2.Pin_0
  N8: Part1.D7, Part3.VCC
  5V: Part1.5V, U1.2, Part2.VCC, U2.2, Part3.OUT, J1.pin2, R3.Pin_1
  GND: Part1.GND, U1.1, Part2.GND, U2.1, Part3.GND, Q1.C, R3.Pin_0, LED1.anode
  N9: U1.9, U1.11, U1.13, U1.15, U1.16, U2.9, U2.11, U2.13, U2.14, U2.15, U2.16
  N10: J1.pin1, Q1.E
  N11: Q1.B, R1.Pin_1
  N12: R2.Pin_1, LED1.cathode

notes:
  Gyro VIO=ADO
  (Wyższy adres)
  Opronik 100 Ohm ze wzgl na powerbank (jeszcze za duży)
  Display 2
  Display 1
